// Logisim project CD4029.circ as structural Verilog: 2 circuits, main circuit CD4029
module Internal_ff (
  input  TE,
  input  PE,
  input  CL,
  input  J,
  output Q,
  output nQ
);

  wire and_1_out, and_2_out, and_3_out, not_1_out;

  and and_1 (and_1_out, PE, ~TE);  // AND_Gate
  and and_2 (and_2_out, ~PE, J);  // AND_Gate
  T_Flip_Flop t_ff_1 (.T(and_1_out), .clk(not_1_out), .Q(Q), .Qn(nQ), .reset(and_3_out), .preset(and_2_out));
  not not_1 (not_1_out, CL);
  and and_3 (and_3_out, ~PE, ~J);  // AND_Gate
endmodule

module CD4029 (
  input  JAM_1,
  input  JAM_2,
  input  JAM_3,
  input  JAM_4,
  input  BINARY_DECADE,
  input  PRESET_ENABLE,
  input  CARRY_IN,
  input  UP_DOWN,
  input  CLOCK,
  output CARRY_OUT,
  output Q1,
  output Q2,
  output Q3,
  output Q4
);

  wire and_1_out, and_2_out, and_3_out, and_4_out, and_5_out, and_6_out, and_7_out, and_8_out, and_9_out,
       and_10_out, and_11_out, and_12_out, and_13_out, and_14_out, and_15_out, FF_1_nq, FF_2_nq,
       internal_ff_1_nq, internal_ff_2_nq, nand_1_out, nand_2_out, nand_3_out, nand_4_out, nor_1_out,
       nor_2_out, nor_3_out, not_1_out, not_2_out, not_3_out, not_4_out, not_5_out, not_6_out, not_7_out,
       not_8_out, not_9_out, not_10_out, not_11_out, or_1_out, or_2_out;

  not not_1 (not_1_out, BINARY_DECADE);
  not not_2 (not_2_out, PRESET_ENABLE);
  not not_3 (not_3_out, CARRY_IN);
  not not_4 (not_4_out, UP_DOWN);
  not not_5 (not_5_out, CLOCK);
  not not_6 (not_6_out, not_1_out);
  not not_7 (not_7_out, not_4_out);
  nand nand_1 (nand_1_out, not_2_out, not_5_out);
  not not_8 (not_8_out, nand_1_out);
  Internal_ff FF_1 (.Q(Q1), .PE(not_2_out), .TE(CARRY_IN), .J(JAM_1), .CL(not_8_out), .nQ(FF_1_nq));
  LED led_1 (.in(Q1));
  nand nand_2 (nand_2_out, not_3_out, not_4_out, FF_1_nq);
  not not_9 (not_9_out, nand_2_out);
  and and_1 (and_1_out, not_11_out, not_9_out);
  and and_2 (and_2_out, not_10_out, nand_4_out);
  nand nand_3 (nand_3_out, Q1, not_3_out, not_7_out);
  not not_10 (not_10_out, nand_3_out);
  not not_11 (not_11_out, and_3_out);
  nor nor_1 (nor_1_out, and_1_out, and_2_out);
  nand nand_4 (nand_4_out, not_1_out, Q4);
  Internal_ff FF_2 (.Q(Q2), .PE(not_2_out), .TE(nor_1_out), .J(JAM_2), .CL(not_8_out), .nQ(FF_2_nq));
  LED led_2 (.in(Q2));
  and and_3 (and_3_out, ~not_6_out, ~Q3, ~Q4, ~Q2);  // AND_Gate
  and and_4 (and_4_out, ~and_3_out, ~Q2);  // AND_Gate
  and and_5 (and_5_out, ~FF_2_nq, ~internal_ff_1_nq);  // AND_Gate
  and and_6 (and_6_out, not_9_out, and_4_out);
  nor nor_2 (nor_2_out, and_6_out, and_7_out);
  and and_7 (and_7_out, Q2, not_10_out);
  or or_1 (or_1_out, and_5_out, ~nand_4_out);  // OR_Gate
  Internal_ff internal_ff_1 (.Q(Q3), .PE(not_2_out), .TE(nor_2_out), .J(JAM_3), .CL(not_8_out), .nQ(internal_ff_1_nq));
  LED led_3 (.in(Q3));
  and and_8 (and_8_out, ~Q2, ~Q3);  // AND_Gate
  and and_9 (and_9_out, not_9_out, and_8_out);
  and and_10 (and_10_out, or_1_out, not_10_out);
  nor nor_3 (nor_3_out, and_9_out, and_10_out);
  and and_11 (and_11_out, ~internal_ff_1_nq, ~FF_2_nq);  // AND_Gate
  or or_2 (or_2_out, ~not_6_out, and_11_out);  // OR_Gate
  and and_12 (and_12_out, ~internal_ff_2_nq, or_2_out);  // AND_Gate
  Internal_ff internal_ff_2 (.Q(Q4), .PE(not_2_out), .TE(nor_3_out), .J(JAM_4), .CL(not_8_out), .nQ(internal_ff_2_nq));
  LED led_4 (.in(Q4));
  and and_13 (and_13_out, ~Q3, ~Q2, ~Q4);  // AND_Gate
  and and_14 (and_14_out, not_9_out, and_13_out);
  and and_15 (and_15_out, and_12_out, not_10_out);
  nor nor_4 (CARRY_OUT, and_14_out, and_15_out);

  // Notes on the sheet:
  //   A
  //   B
  //   C
  //   D
  //   E
  //   F
  //   G
  //   H
  //   I
  //   J
  //   K
  //   L
endmodule
